# Fritzing sketch Bus (saved by Fritzing 0.9.3b)
stripboards: 1

parts:
  Uno = Arduino Uno (Rev3) - ICSP
  RFID = RFID-RC522-v3
  WeMos = WeMos D1 Mini
  Buzzer = Piezo Speaker
  LCD = LCD screen
  R1 = Trimmer Potentiometer [maximum_resistance=10kΩ package=THT]
  R2 = Resistor [tolerance=±5% resistance=220 package=THT]

nets:
  N1: Uno.D10_PWM/SS, Buzzer.pin2
  N2: Uno.D11_PWM/MOSI, LCD.E
  N3: Uno.D12/MISO, LCD.RS
  GND: Uno.GND, Buzzer.pin1, LCD.VSS, LCD.R/W, LCD.LED-, R1.leg1
  N4: Uno.D0/RX, WeMos.TX
  N5: Uno.D1/TX, WeMos.RX
  N6: Uno.D2, LCD.DB7
  N7: Uno.D3_PWM, LCD.DB6
  N8: Uno.D4, LCD.DB5
  N9: Uno.D5_PWM, LCD.DB4
  5V: Uno.5V, LCD.VDD, R1.leg2, R2.Pin_0
  N10: RFID.SDA, WeMos.D8
  N11: RFID.SCK, WeMos.D5
  N12: RFID.MOSI, WeMos.D7
  N13: RFID.MISO, WeMos.D6
  N14: RFID.GND, WeMos.G
  N15: RFID.RST, WeMos.D3
  3.3V: RFID.3.3V, WeMos.3V3
  N16: LCD.V0, R1.wiper
  N17: LCD.LED+, R2.Pin_1

custom parts:
  RFID-RC522-v3: A simple China made RFID-RC522 Reader (6x4 cm); do check the pin labels, as this is a MFRC522 based clone.
